# Fritzing sketch wiringLinkit (saved by Fritzing 0.9.3b)

parts:
  INA1 = INA219 DC Current Sensor Breakout
  LED1 = smd LED [color="Green (555nm)" package="0805 [SMD]"]
  LED2 = LED - 5mm [color="Red (633nm)" package="5 mm [THT]"]
  S1 = Round Pushbutton
  Power_plug1 = Power plug
  Part1 = LinkIt Smart 7688 Duo

nets:
  VCC: INA1.VCC, Part1.3V3
  GND: INA1.GND, LED1.cathode, LED2.cathode, S1.leg1, Part1.GND
  N1: INA1.SCL, Part1.D3
  N2: INA1.SDA, Part1.D2
  N3: INA1.Vin+2, Power_plug1.VCC
  N4: LED1.anode, Part1.D8
  N5: LED2.anode, Part1.D9
  N6: S1.leg0, Part1.D7

notes:
  3.3V

custom parts:
  INA219 DC Current Sensor Breakout: INA DC Current Sensor Breakout
  LinkIt Smart 7688 Duo: At the heart of the platform is the MT7688AN SOC, an appliance automation bridge. This chipset is based on a powerful 802.11n 1T1R Wi-Fi AP, supports up to 2Gb RAM with additional SD-card storage, encryption engine Wi-Fi and a wide variety of peripheral connectivity options.
